// Logisim project cpu.circ as structural Verilog: 5 circuits, main circuit main
module main (
  input  [31:0] INSTRUCTION,
  input  CLOCK,
  output [31:0] PROGRAM_COUNTER,
  output [31:0] ra,
  output [31:0] sp,
  output [31:0] t0,
  output [31:0] t1,
  output [31:0] t2,
  output [31:0] s0,
  output [31:0] s1,
  output [31:0] a0
);

  wire ASel, BrEq, BrLt, BrUn, BSel, MemRW, PCSel, RegWEn;
  wire [1:0] LSel, WBSel;
  wire [2:0] ImmSel;
  wire [3:0] ALUSel;
  wire [31:0] ALUout, DMEM_p5, dmoutputer_1_result, imgenerator_1_result, IR, IR2, multiplexer_1_out,
       multiplexer_3_out, multiplexer_4_out, PC2, PC4, PC24, RegFile_read_data_1, RegFile_read_data_2, wb;

  Multiplexer #(.width(32), .enable("false")) multiplexer_1 (
    .in0(PC4), .in1(ALUout), .out(multiplexer_1_out), .sel(PCSel));
  Register #(.width(32)) PC (.D(multiplexer_1_out), .en(1'b1), .clk(CLOCK), .Q(PROGRAM_COUNTER));  // open: clr
  Adder #(.width(32)) adder_1 (.a(PROGRAM_COUNTER), .b(32'h4), .out(PC4));  // open: cin, cout
  Register #(.width(32)) register_1 (.D(IR2), .en(1'b1), .clk(CLOCK), .Q(IR));  // open: clr
  LogicControl logiccontrol_1 (
    .instr(IR), .BrEq(BrEq), .BrLt(BrLt), .ImmSel(ImmSel), .PCSel(PCSel), .ASel(ASel), .ALUSel(ALUSel),
    .MemRW(MemRW), .RegWEn(RegWEn), .BrUn(BrUn), .BSel(BSel), .LSel(LSel), .WBSel(WBSel));
  Multiplexer #(.width(32), .enable("false")) multiplexer_2 (.in0(INSTRUCTION), .in1(32'h13), .out(IR2), .sel(PCSel));
  Register #(.width(32)) register_2 (.D(PROGRAM_COUNTER), .en(1'b1), .clk(CLOCK), .Q(PC2));  // open: clr
  IMGenerator imgenerator_1 (.A(IR), .ImmSel(ImmSel), .RESULT(imgenerator_1_result));
  regfile_main RegFile (
    .rs2(IR[24:20]), .rd(IR[11:7]), .Read_Data_1(RegFile_read_data_1), .Read_Data_2(RegFile_read_data_2),
    .ra(ra), .sp(sp), .t0(t0), .t1(t1), .t2(t2), .s0(s0), .s1(s1), .a0(a0), .rs1(IR[19:15]), .Write_Data(wb),
    .RegWEn(RegWEn), .clk(CLOCK));
  BranchComp branchcomp_1 (.rs1(RegFile_read_data_1), .rs2(RegFile_read_data_2), .BrUn(BrUn), .BrEq(BrEq), .BrLt(BrLt));
  Multiplexer #(.width(32), .enable("false")) multiplexer_3 (
    .in0(RegFile_read_data_2), .in1(imgenerator_1_result), .out(multiplexer_3_out), .sel(BSel));
  Multiplexer #(.width(32), .enable("false")) multiplexer_4 (
    .in0(RegFile_read_data_1), .in1(PC2), .out(multiplexer_4_out), .sel(ASel));
  alu Arithmetic_Logic_Unit (.Result(ALUout), .ALUSel(ALUSel), .A(multiplexer_4_out), .B(multiplexer_3_out));
  // mem_main DMEM: pin names not known; wires that end beside it: ALUout, RegFile_read_data_2, CLOCK, MemRW, DMEM_p5
  DMOutputer dmoutputer_1 (.A(DMEM_p5), .LSel(LSel), .RESULT(dmoutputer_1_result));
  Adder #(.width(32)) adder_2 (.a(PC2), .b(32'h4), .out(PC24));  // open: cin, cout
  Multiplexer #(.select(2), .width(32), .enable("false")) multiplexer_5 (
    .in0(PC24), .in1(ALUout), .in2(dmoutputer_1_result), .out(wb), .sel(WBSel));  // open: in3

  // Other names for the same wires on the sheet: clk = CLOCK

  // Notes on the sheet:
  //   Output
  //   IMEM (do **NOT** move this)
  //   Inputs
  //   It is OK to move the PC, RegFile, ALU, and MEM to wherever is most convenient for you when constructing your CPU, and to delete this text
  //   Inputs/Outputs for testing. Do **NOT** move these.
endmodule

module IMGenerator (
  input  [31:0] A,
  input  [2:0] ImmSel,
  output [31:0] RESULT
);

  wire [31:0] adder_1_out, adder_2_out, adder_3_out, adder_4_out, adder_5_out, adder_6_out, adder_7_out,
       adder_8_out, adder_9_out, bit_extender_1_out, bit_extender_2_out, bit_extender_3_out,
       bit_extender_4_out, bit_extender_5_out, bit_extender_6_out, bit_extender_7_out, bit_extender_8_out,
       bit_extender_9_out, bit_extender_10_out, bit_extender_11_out, bit_extender_12_out,
       bit_extender_13_out, bit_extender_14_out, bit_extender_15_out, demultiplexer_1_out0,
       demultiplexer_1_out1, demultiplexer_1_out2, demultiplexer_1_out3, demultiplexer_1_out4,
       demultiplexer_1_out5, demultiplexer_1_out6, shifter_1_out, shifter_2_out, shifter_3_out,
       shifter_4_out, shifter_5_out, shifter_6_out, shifter_7_out, shifter_8_out, shifter_9_out,
       shifter_10_out, shifter_11_out, shifter_12_out;

  Demultiplexer #(.select(3), .width(32), .enable("false")) demultiplexer_1 (
    .out0(demultiplexer_1_out0), .out1(demultiplexer_1_out1), .out2(demultiplexer_1_out2),
    .out3(demultiplexer_1_out3), .out4(demultiplexer_1_out4), .out5(demultiplexer_1_out5),
    .out6(demultiplexer_1_out6), .in(A), .sel(ImmSel));  // open: out7
  assign bit_extender_1_out = {{12{demultiplexer_1_out4[31]}}, demultiplexer_1_out4[31:12]};  // Bit_Extender bit_extender_1
  assign bit_extender_2_out = {{20{demultiplexer_1_out1[31]}}, demultiplexer_1_out1[31:20]};  // Bit_Extender bit_extender_2
  assign bit_extender_3_out = {{28{1'b0}}, demultiplexer_1_out2[11:8]};  // Bit_Extender bit_extender_3
  assign bit_extender_4_out = {{25{demultiplexer_1_out2[31]}}, demultiplexer_1_out2[31:25]};  // Bit_Extender bit_extender_4
  assign bit_extender_5_out = {{28{1'b0}}, demultiplexer_1_out3[11:8]};  // Bit_Extender bit_extender_5
  assign bit_extender_6_out = {{26{1'b0}}, demultiplexer_1_out3[30:25]};  // Bit_Extender bit_extender_6
  assign bit_extender_7_out = {{31{1'b0}}, demultiplexer_1_out3[7]};  // Bit_Extender bit_extender_7
  assign bit_extender_8_out = {{31{demultiplexer_1_out3[31]}}, demultiplexer_1_out3[31]};  // Bit_Extender bit_extender_8
  Shifter #(.width(32)) shifter_1 (.in(bit_extender_1_out), .\dist (5'b01100), .out(shifter_1_out));
  assign bit_extender_9_out = {{28{1'b0}}, demultiplexer_1_out5[24:21]};  // Bit_Extender bit_extender_9
  assign bit_extender_10_out = {{26{1'b0}}, demultiplexer_1_out5[30:25]};  // Bit_Extender bit_extender_10
  assign bit_extender_11_out = {{31{1'b0}}, demultiplexer_1_out5[20]};  // Bit_Extender bit_extender_11
  assign bit_extender_12_out = {{24{1'b0}}, demultiplexer_1_out5[19:12]};  // Bit_Extender bit_extender_12
  assign bit_extender_13_out = {{31{demultiplexer_1_out5[31]}}, demultiplexer_1_out5[31]};  // Bit_Extender bit_extender_13
  assign bit_extender_14_out = {{27{demultiplexer_1_out6[24]}}, demultiplexer_1_out6[24:20]};  // Bit_Extender bit_extender_14
  assign bit_extender_15_out = {{31{1'b0}}, demultiplexer_1_out2[7]};  // Bit_Extender bit_extender_15
  Shifter #(.width(32)) shifter_2 (.in(bit_extender_9_out), .\dist (5'b00001), .out(shifter_2_out));
  Shifter #(.width(32)) shifter_3 (.in(bit_extender_10_out), .\dist (5'b00101), .out(shifter_3_out));
  Shifter #(.width(32)) shifter_4 (.in(bit_extender_11_out), .\dist (5'b01011), .out(shifter_4_out));
  Shifter #(.width(32)) shifter_5 (.in(bit_extender_12_out), .\dist (5'b01100), .out(shifter_5_out));
  Shifter #(.width(32)) shifter_6 (.in(bit_extender_13_out), .\dist (5'b10100), .out(shifter_6_out));
  Shifter #(.width(32)) shifter_7 (.in(bit_extender_3_out), .\dist (5'b00001), .out(shifter_7_out));
  Shifter #(.width(32)) shifter_8 (.in(bit_extender_4_out), .\dist (5'b00101), .out(shifter_8_out));
  Shifter #(.width(32)) shifter_9 (.in(bit_extender_5_out), .\dist (5'b00001), .out(shifter_9_out));
  Shifter #(.width(32)) shifter_10 (.in(bit_extender_6_out), .\dist (5'b00101), .out(shifter_10_out));
  Shifter #(.width(32)) shifter_11 (.in(bit_extender_7_out), .\dist (5'b01011), .out(shifter_11_out));
  Shifter #(.width(32)) shifter_12 (.in(bit_extender_8_out), .\dist (5'b01100), .out(shifter_12_out));
  Adder #(.width(32)) adder_1 (.a(bit_extender_15_out), .b(shifter_7_out), .out(adder_1_out));  // open: cin, cout
  Adder #(.width(32)) adder_2 (.a(shifter_9_out), .b(shifter_10_out), .out(adder_2_out));  // open: cin, cout
  Adder #(.width(32)) adder_3 (.a(shifter_11_out), .b(shifter_12_out), .out(adder_3_out));  // open: cin, cout
  Adder #(.width(32)) adder_4 (.a(shifter_2_out), .b(shifter_3_out), .out(adder_4_out));  // open: cin, cout
  Adder #(.width(32)) adder_5 (.a(shifter_4_out), .b(shifter_5_out), .out(adder_5_out));  // open: cin, cout
  Adder #(.width(32)) adder_6 (.a(adder_1_out), .b(shifter_8_out), .out(adder_6_out));  // open: cin, cout
  Adder #(.width(32)) adder_7 (.a(adder_2_out), .b(adder_3_out), .out(adder_7_out));  // open: cin, cout
  Adder #(.width(32)) adder_8 (.a(adder_4_out), .b(adder_5_out), .out(adder_8_out));  // open: cin, cout
  Adder #(.width(32)) adder_9 (.a(adder_8_out), .b(shifter_6_out), .out(adder_9_out));  // open: cin, cout
  Multiplexer #(.select(3), .width(32), .enable("false")) multiplexer_1 (
    .in0(demultiplexer_1_out0), .in1(bit_extender_2_out), .in2(adder_6_out), .in3(adder_7_out),
    .in4(shifter_1_out), .in5(adder_9_out), .in6(bit_extender_14_out), .out(RESULT), .sel(ImmSel));  // open: in7
endmodule

module BranchComp (
  input  [31:0] rs1,
  input  [31:0] rs2,
  input  BrUn,
  output BrEq,
  output BrLt
);

  wire comparator_1_eq, comparator_1_lt, comparator_2_eq, comparator_2_lt;
  wire [31:0] demultiplexer_1_out0, demultiplexer_1_out1, demultiplexer_2_out0, demultiplexer_2_out1;

  Demultiplexer #(.width(32), .enable("false")) demultiplexer_1 (
    .out0(demultiplexer_1_out0), .out1(demultiplexer_1_out1), .in(rs1), .sel(BrUn));
  Demultiplexer #(.width(32), .enable("false")) demultiplexer_2 (
    .out0(demultiplexer_2_out0), .out1(demultiplexer_2_out1), .in(rs2), .sel(BrUn));
  Comparator #(.width(32)) comparator_1 (
    .a(demultiplexer_1_out0), .b(demultiplexer_2_out0), .eq(comparator_1_eq), .lt(comparator_1_lt));  // open: gt
  Comparator #(.width(32), .mode("unsigned")) comparator_2 (
    .a(demultiplexer_1_out1), .b(demultiplexer_2_out1), .eq(comparator_2_eq), .lt(comparator_2_lt));  // open: gt
  Multiplexer #(.enable("false")) multiplexer_1 (.in0(comparator_1_eq), .in1(comparator_2_eq), .out(BrEq), .sel(BrUn));
  Multiplexer #(.enable("false")) multiplexer_2 (.in0(comparator_1_lt), .in1(comparator_2_lt), .out(BrLt), .sel(BrUn));
endmodule

module DMOutputer (
  input  [31:0] A,
  input  [1:0] LSel,
  output [31:0] RESULT
);

  wire [31:0] bit_extender_1_out, bit_extender_2_out, demultiplexer_1_out0, demultiplexer_1_out1,
       demultiplexer_1_out2;

  Demultiplexer #(.select(2), .width(32), .enable("false")) demultiplexer_1 (
    .out0(demultiplexer_1_out0), .out1(demultiplexer_1_out1), .out2(demultiplexer_1_out2), .in(A), .sel(LSel));  // open: out3
  assign bit_extender_1_out = {{16{demultiplexer_1_out1[31]}}, demultiplexer_1_out1[31:16]};  // Bit_Extender bit_extender_1
  assign bit_extender_2_out = {{24{demultiplexer_1_out2[31]}}, demultiplexer_1_out2[31:24]};  // Bit_Extender bit_extender_2
  Multiplexer #(.select(2), .width(32), .enable("false")) multiplexer_1 (
    .in0(demultiplexer_1_out0), .in1(bit_extender_1_out), .in2(bit_extender_2_out), .out(RESULT), .sel(LSel));  // open: in3
endmodule

module LogicControl (
  input  [31:0] instr,
  input  BrEq,
  input  BrLt,
  output [2:0] ImmSel,
  output PCSel,
  output ASel,
  output [3:0] ALUSel,
  output MemRW,
  output RegWEn,
  output BrUn,
  output BSel,
  output [1:0] LSel,
  output [1:0] WBSel
);

  wire add0, addi0, addx_out, and0, and_1_out, and_2_out, and_3_out, and_4_out, and_5_out, andi0, andx_out,
       beq0, blt0, bne0, divu0, IStype, Itype, jal0, jalr0, lb0, lh0, lui0, lw0, mul0, mulh0, mulhu0,
       not_1_out, not_2_out, not_3_out, not_4_out, not_5_out, not_6_out, not_7_out, not_8_out, not_9_out,
       not_10_out, not_11_out, not_12_out, not_13_out, not_14_out, not_15_out, not_16_out, not_17_out,
       not_18_out, not_19_out, not_20_out, not_21_out, not_22_out, not_23_out, not_24_out, not_25_out,
       not_26_out, not_27_out, not_28_out, not_29_out, not_30_out, not_31_out, not_32_out, not_33_out,
       not_34_out, not_35_out, not_36_out, not_37_out, not_38_out, not_39_out, not_40_out, not_41_out,
       not_42_out, not_43_out, not_44_out, not_45_out, not_46_out, not_47_out, not_48_out, not_49_out,
       not_50_out, not_51_out, not_52_out, not_53_out, not_54_out, not_55_out, not_56_out, not_57_out,
       not_58_out, not_59_out, not_60_out, not_61_out, not_62_out, not_63_out, not_64_out, not_65_out,
       not_66_out, not_67_out, not_68_out, not_69_out, not_70_out, not_71_out, not_72_out, not_73_out,
       not_74_out, not_75_out, not_76_out, not_77_out, not_78_out, not_79_out, not_80_out, not_81_out,
       not_82_out, not_83_out, not_84_out, not_85_out, not_86_out, not_87_out, not_88_out, not_89_out,
       not_90_out, not_91_out, not_92_out, not_93_out, not_94_out, not_95_out, not_96_out, not_97_out,
       not_98_out, not_99_out, not_100_out, not_101_out, not_102_out, not_103_out, not_104_out, not_105_out,
       not_106_out, not_107_out, not_108_out, not_109_out, not_110_out, not_111_out, not_112_out,
       not_113_out, not_114_out, not_115_out, not_116_out, not_117_out, not_118_out, not_119_out,
       not_120_out, not_121_out, not_122_out, not_123_out, not_124_out, not_125_out, not_126_out,
       not_127_out, not_128_out, not_129_out, not_130_out, not_131_out, not_132_out, not_133_out,
       not_134_out, not_135_out, not_136_out, not_137_out, not_138_out, not_139_out, not_140_out,
       not_141_out, not_142_out, not_143_out, not_144_out, not_145_out, not_146_out, not_147_out,
       not_148_out, not_149_out, not_150_out, not_151_out, not_152_out, not_153_out, not_154_out,
       not_155_out, not_156_out, not_157_out, not_158_out, not_159_out, not_160_out, not_161_out,
       not_162_out, not_163_out, not_164_out, not_165_out, not_166_out, not_167_out, not_168_out,
       not_169_out, not_170_out, not_171_out, not_172_out, not_173_out, not_174_out, not_175_out,
       not_176_out, not_177_out, not_178_out, not_179_out, not_180_out, not_181_out, not_182_out,
       not_183_out, not_184_out, not_185_out, not_186_out, not_187_out, not_188_out, not_189_out,
       not_190_out, not_191_out, not_192_out, not_193_out, not_194_out, not_195_out, not_196_out,
       not_197_out, not_198_out, not_199_out, not_200_out, not_201_out, not_202_out, not_203_out,
       not_204_out, not_205_out, not_206_out, not_207_out, not_208_out, not_209_out, not_210_out,
       not_211_out, not_212_out, not_213_out, not_214_out, not_215_out, not_216_out, not_217_out,
       not_218_out, not_219_out, not_220_out, not_221_out, not_222_out, not_223_out, not_224_out,
       not_225_out, not_226_out, not_227_out, not_228_out, not_229_out, not_230_out, not_231_out,
       not_232_out, not_233_out, not_234_out, not_235_out, not_236_out, not_237_out, not_238_out,
       not_239_out, not_240_out, not_241_out, not_242_out, not_243_out, not_244_out, not_245_out,
       not_246_out, not_247_out, not_248_out, not_249_out, not_250_out, not_251_out, not_252_out,
       not_253_out, not_254_out, not_255_out, not_256_out, not_257_out, not_258_out, not_259_out,
       not_260_out, not_261_out, not_262_out, not_263_out, not_264_out, not_265_out, not_266_out, or0,
       or_9_out, or_10_out, or_11_out, ori0, orx_out, remu0, Rtype, SBtype, sll0, slli0, sllx_out, slt0,
       slti0, sltx_out, srai0, srl0, srli0, srlx_out, sub0, xor0, xori0, xorx_out;

  not not_1 (not_1_out, BrEq);
  and and_1 (and_1_out, beq0, BrEq);
  and and_2 (and_2_out, blt0, BrLt);
  and and_3 (and_3_out, BrUn, BrLt);
  and and_4 (and_4_out, bne0, not_1_out);
  and and_5 (and_5_out, slti0, BrLt);
  Priority_Encoder priority_encoder_1 (
    .in0(Rtype), .in1(Itype), .in2(MemRW), .in3(SBtype), .in4(lui0), .in5(jal0), .in6(IStype), .out(ImmSel));  // open: in7, en_in, gs, en_out
  or or_1 (Rtype, add0, mul0, sub0, sll0, mulh0, mulhu0, slt0, xor0, divu0, srl0, or0, remu0, and0);
  or or_2 (SBtype, beq0, blt0, BrUn, bne0);
  or or_3 (Itype, slti0, lb0, lh0, lw0, addi0, xori0, ori0, andi0, jalr0);
  or or_4 (IStype, slli0, srli0, srai0);
  or or_5 (PCSel, and_1_out, and_2_out, and_3_out, and_4_out, jal0, jalr0);
  or or_6 (RegWEn, add0, mul0, sub0, sll0, mulh0, mulhu0, slt0, xor0, divu0, srl0, or0, remu0, and0, and_5_out, lb0, lh0, lw0, addi0, xori0, ori0, andi0, jalr0, lui0, jal0, slli0, srli0, srai0);
  not not_2 (not_2_out, instr[2]);
  not not_3 (not_3_out, instr[3]);
  not not_4 (not_4_out, instr[6]);
  not not_5 (not_5_out, instr[12]);
  not not_6 (not_6_out, instr[13]);
  not not_7 (not_7_out, instr[14]);
  not not_8 (not_8_out, instr[25]);
  not not_9 (not_9_out, instr[26]);
  not not_10 (not_10_out, instr[27]);
  not not_11 (not_11_out, instr[28]);
  not not_12 (not_12_out, instr[29]);
  not not_13 (not_13_out, instr[30]);
  not not_14 (not_14_out, instr[31]);
  not not_15 (not_15_out, instr[2]);
  not not_16 (not_16_out, instr[3]);
  not not_17 (not_17_out, instr[6]);
  not not_18 (not_18_out, instr[12]);
  not not_19 (not_19_out, instr[14]);
  not not_20 (not_20_out, instr[25]);
  not not_21 (not_21_out, instr[26]);
  not not_22 (not_22_out, instr[27]);
  not not_23 (not_23_out, instr[28]);
  not not_24 (not_24_out, instr[29]);
  not not_25 (not_25_out, instr[30]);
  not not_26 (not_26_out, instr[31]);
  not not_27 (not_27_out, instr[2]);
  not not_28 (not_28_out, instr[3]);
  not not_29 (not_29_out, instr[6]);
  not not_30 (not_30_out, instr[25]);
  not not_31 (not_31_out, instr[26]);
  not not_32 (not_32_out, instr[27]);
  not not_33 (not_33_out, instr[28]);
  not not_34 (not_34_out, instr[29]);
  not not_35 (not_35_out, instr[30]);
  not not_36 (not_36_out, instr[31]);
  not not_37 (not_37_out, instr[2]);
  not not_38 (not_38_out, instr[3]);
  not not_39 (not_39_out, instr[5]);
  not not_40 (not_40_out, instr[6]);
  not not_41 (not_41_out, instr[12]);
  not not_42 (not_42_out, instr[14]);
  not not_43 (not_43_out, instr[2]);
  not not_44 (not_44_out, instr[3]);
  not not_45 (not_45_out, instr[4]);
  not not_46 (not_46_out, instr[6]);
  not not_47 (not_47_out, instr[12]);
  not not_48 (not_48_out, instr[14]);
  not not_49 (not_49_out, instr[4]);
  and and_6 (add0, instr[0], instr[1], not_2_out, not_3_out, instr[4], instr[5], not_4_out, not_5_out, not_6_out, not_7_out, not_8_out, not_9_out, not_10_out, not_11_out, not_12_out, not_13_out, not_14_out);
  and and_7 (slt0, instr[0], instr[1], not_15_out, not_16_out, instr[4], instr[5], not_17_out, not_18_out, instr[13], not_19_out, not_20_out, not_21_out, not_22_out, not_23_out, not_24_out, not_25_out, not_26_out);
  and and_8 (and0, instr[0], instr[1], not_27_out, not_28_out, instr[4], instr[5], not_29_out, instr[12], instr[13], instr[14], not_30_out, not_31_out, not_32_out, not_33_out, not_34_out, not_35_out, not_36_out);
  and and_9 (slti0, instr[0], instr[1], not_37_out, not_38_out, instr[4], not_39_out, not_40_out, not_41_out, instr[13], not_42_out);
  and and_10 (MemRW, instr[0], instr[1], not_43_out, not_44_out, not_45_out, instr[5], not_46_out, not_47_out, instr[13], not_48_out);
  and and_11 (jal0, instr[0], instr[1], instr[2], instr[3], not_49_out, instr[5], instr[6]);
  not not_50 (not_50_out, instr[2]);
  not not_51 (not_51_out, instr[3]);
  not not_52 (not_52_out, instr[6]);
  not not_53 (not_53_out, instr[12]);
  not not_54 (not_54_out, instr[13]);
  not not_55 (not_55_out, instr[14]);
  not not_56 (not_56_out, instr[26]);
  not not_57 (not_57_out, instr[27]);
  not not_58 (not_58_out, instr[28]);
  not not_59 (not_59_out, instr[29]);
  not not_60 (not_60_out, instr[30]);
  not not_61 (not_61_out, instr[31]);
  not not_62 (not_62_out, instr[2]);
  not not_63 (not_63_out, instr[3]);
  not not_64 (not_64_out, instr[6]);
  not not_65 (not_65_out, instr[12]);
  not not_66 (not_66_out, instr[13]);
  not not_67 (not_67_out, instr[25]);
  not not_68 (not_68_out, instr[26]);
  not not_69 (not_69_out, instr[27]);
  not not_70 (not_70_out, instr[28]);
  not not_71 (not_71_out, instr[29]);
  not not_72 (not_72_out, instr[30]);
  not not_73 (not_73_out, instr[31]);
  not not_74 (not_74_out, instr[2]);
  not not_75 (not_75_out, instr[3]);
  not not_76 (not_76_out, instr[4]);
  not not_77 (not_77_out, instr[5]);
  not not_78 (not_78_out, instr[6]);
  not not_79 (not_79_out, instr[12]);
  not not_80 (not_80_out, instr[13]);
  not not_81 (not_81_out, instr[14]);
  not not_82 (not_82_out, instr[2]);
  not not_83 (not_83_out, instr[3]);
  not not_84 (not_84_out, instr[5]);
  not not_85 (not_85_out, instr[6]);
  not not_86 (not_86_out, instr[12]);
  not not_87 (not_87_out, instr[13]);
  not not_88 (not_88_out, instr[2]);
  not not_89 (not_89_out, instr[3]);
  not not_90 (not_90_out, instr[4]);
  not not_91 (not_91_out, instr[12]);
  not not_92 (not_92_out, instr[13]);
  not not_93 (not_93_out, instr[14]);
  not not_94 (not_94_out, instr[3]);
  not not_95 (not_95_out, instr[4]);
  not not_96 (not_96_out, instr[12]);
  not not_97 (not_97_out, instr[13]);
  not not_98 (not_98_out, instr[14]);
  or or_7 (BSel, slti0, lb0, lh0, lw0, addi0, xori0, ori0, andi0, jalr0, MemRW, beq0, blt0, BrUn, bne0, lui0, jal0, slli0, srli0, srai0);
  and and_12 (mul0, instr[0], instr[1], not_50_out, not_51_out, instr[4], instr[5], not_52_out, not_53_out, not_54_out, not_55_out, instr[25], not_56_out, not_57_out, not_58_out, not_59_out, not_60_out, not_61_out);
  and and_13 (xor0, instr[0], instr[1], not_62_out, not_63_out, instr[4], instr[5], not_64_out, not_65_out, not_66_out, instr[14], not_67_out, not_68_out, not_69_out, not_70_out, not_71_out, not_72_out, not_73_out);
  and and_14 (lb0, instr[0], instr[1], not_74_out, not_75_out, not_76_out, not_77_out, not_78_out, not_79_out, not_80_out, not_81_out);
  and and_15 (xori0, instr[0], instr[1], not_82_out, not_83_out, instr[4], not_84_out, not_85_out, not_86_out, not_87_out, instr[14]);
  and and_16 (beq0, instr[0], instr[1], not_88_out, not_89_out, not_90_out, instr[5], instr[6], not_91_out, not_92_out, not_93_out);
  and and_17 (jalr0, instr[0], instr[1], instr[2], not_94_out, not_95_out, instr[5], instr[6], not_96_out, not_97_out, not_98_out);
  not not_99 (not_99_out, instr[4]);
  not not_100 (not_100_out, instr[5]);
  not not_101 (not_101_out, instr[2]);
  not not_102 (not_102_out, instr[3]);
  not not_103 (not_103_out, instr[5]);
  not not_104 (not_104_out, instr[6]);
  not not_105 (not_105_out, instr[13]);
  not not_106 (not_106_out, instr[25]);
  not not_107 (not_107_out, instr[26]);
  not not_108 (not_108_out, instr[27]);
  not not_109 (not_109_out, instr[28]);
  not not_110 (not_110_out, instr[29]);
  not not_111 (not_111_out, instr[30]);
  not not_112 (not_112_out, instr[31]);
  not not_113 (not_113_out, instr[2]);
  not not_114 (not_114_out, instr[3]);
  not not_115 (not_115_out, instr[4]);
  not not_116 (not_116_out, instr[12]);
  not not_117 (not_117_out, instr[13]);
  not not_118 (not_118_out, instr[2]);
  not not_119 (not_119_out, instr[3]);
  not not_120 (not_120_out, instr[6]);
  not not_121 (not_121_out, instr[12]);
  not not_122 (not_122_out, instr[13]);
  not not_123 (not_123_out, instr[14]);
  not not_124 (not_124_out, instr[25]);
  not not_125 (not_125_out, instr[26]);
  not not_126 (not_126_out, instr[27]);
  not not_127 (not_127_out, instr[28]);
  not not_128 (not_128_out, instr[29]);
  not not_129 (not_129_out, instr[31]);
  not not_130 (not_130_out, instr[2]);
  not not_131 (not_131_out, instr[3]);
  not not_132 (not_132_out, instr[6]);
  not not_133 (not_133_out, instr[13]);
  not not_134 (not_134_out, instr[26]);
  not not_135 (not_135_out, instr[27]);
  not not_136 (not_136_out, instr[28]);
  not not_137 (not_137_out, instr[29]);
  not not_138 (not_138_out, instr[30]);
  not not_139 (not_139_out, instr[31]);
  not not_140 (not_140_out, instr[2]);
  not not_141 (not_141_out, instr[3]);
  not not_142 (not_142_out, instr[6]);
  not not_143 (not_143_out, instr[13]);
  not not_144 (not_144_out, instr[14]);
  or or_8 (ASel, beq0, blt0, BrUn, bne0, jal0);
  and and_18 (sub0, instr[0], instr[1], not_118_out, not_119_out, instr[4], instr[5], not_120_out, not_121_out, not_122_out, not_123_out, not_124_out, not_125_out, not_126_out, not_127_out, not_128_out, instr[30], not_129_out);
  and and_19 (divu0, instr[0], instr[1], not_130_out, not_131_out, instr[4], instr[5], not_132_out, instr[12], not_133_out, instr[14], instr[25], not_134_out, not_135_out, not_136_out, not_137_out, not_138_out, not_139_out);
  and and_20 (lh0, instr[0], instr[1], not_140_out, not_141_out, not_99_out, not_100_out, not_142_out, instr[12], not_143_out, not_144_out);
  and and_21 (srli0, instr[0], instr[1], not_101_out, not_102_out, instr[4], not_103_out, not_104_out, instr[12], not_105_out, instr[14], not_106_out, not_107_out, not_108_out, not_109_out, not_110_out, not_111_out, not_112_out);
  and and_22 (blt0, instr[0], instr[1], not_113_out, not_114_out, not_115_out, instr[5], instr[6], not_116_out, not_117_out, instr[14]);
  not not_145 (not_145_out, instr[2]);
  not not_146 (not_146_out, instr[3]);
  not not_147 (not_147_out, instr[6]);
  not not_148 (not_148_out, instr[13]);
  not not_149 (not_149_out, instr[14]);
  not not_150 (not_150_out, instr[25]);
  not not_151 (not_151_out, instr[26]);
  not not_152 (not_152_out, instr[27]);
  not not_153 (not_153_out, instr[28]);
  not not_154 (not_154_out, instr[29]);
  not not_155 (not_155_out, instr[30]);
  not not_156 (not_156_out, instr[31]);
  not not_157 (not_157_out, instr[2]);
  not not_158 (not_158_out, instr[3]);
  not not_159 (not_159_out, instr[6]);
  not not_160 (not_160_out, instr[13]);
  not not_161 (not_161_out, instr[25]);
  not not_162 (not_162_out, instr[26]);
  not not_163 (not_163_out, instr[27]);
  not not_164 (not_164_out, instr[28]);
  not not_165 (not_165_out, instr[29]);
  not not_166 (not_166_out, instr[30]);
  not not_167 (not_167_out, instr[31]);
  not not_168 (not_168_out, instr[2]);
  not not_169 (not_169_out, instr[3]);
  not not_170 (not_170_out, instr[4]);
  not not_171 (not_171_out, instr[5]);
  not not_172 (not_172_out, instr[6]);
  not not_173 (not_173_out, instr[12]);
  not not_174 (not_174_out, instr[14]);
  not not_175 (not_175_out, instr[2]);
  not not_176 (not_176_out, instr[3]);
  not not_177 (not_177_out, instr[5]);
  not not_178 (not_178_out, instr[6]);
  not not_179 (not_179_out, instr[13]);
  not not_180 (not_180_out, instr[25]);
  not not_181 (not_181_out, instr[26]);
  not not_182 (not_182_out, instr[27]);
  not not_183 (not_183_out, instr[28]);
  not not_184 (not_184_out, instr[29]);
  not not_185 (not_185_out, instr[31]);
  not not_186 (not_186_out, instr[2]);
  not not_187 (not_187_out, instr[3]);
  not not_188 (not_188_out, instr[4]);
  not not_189 (not_189_out, instr[12]);
  and and_23 (sll0, instr[0], instr[1], not_145_out, not_146_out, instr[4], instr[5], not_147_out, instr[12], not_148_out, not_149_out, not_150_out, not_151_out, not_152_out, not_153_out, not_154_out, not_155_out, not_156_out);
  and and_24 (srl0, instr[0], instr[1], not_157_out, not_158_out, instr[4], instr[5], not_159_out, instr[12], not_160_out, instr[14], not_161_out, not_162_out, not_163_out, not_164_out, not_165_out, not_166_out, not_167_out);
  and and_25 (lw0, instr[0], instr[1], not_168_out, not_169_out, not_170_out, not_171_out, not_172_out, not_173_out, instr[13], not_174_out);
  and and_26 (srai0, instr[0], instr[1], not_175_out, not_176_out, instr[4], not_177_out, not_178_out, instr[12], not_179_out, instr[14], not_180_out, not_181_out, not_182_out, not_183_out, not_184_out, instr[30], not_185_out);
  and and_27 (BrUn, instr[0], instr[1], not_186_out, not_187_out, not_188_out, instr[5], instr[6], not_189_out, instr[13], instr[14]);
  or addx (addx_out, add0, lb0, lh0, lw0, addi0, MemRW, beq0, blt0, BrUn, bne0, lui0, jal0, jalr0);
  or andx (andx_out, and0, andi0);
  or orx (orx_out, or0, ori0);
  or xorx (xorx_out, xor0, xori0);
  or srlx (srlx_out, srl0, srli0);
  or sllx (sllx_out, sll0, slli0);
  or sltx (sltx_out, slt0, slti0);
  Priority_Encoder #(.select(4)) priority_encoder_2 (
    .in0(addx_out), .in1(andx_out), .in2(orx_out), .in3(xorx_out), .in4(srlx_out), .in5(srai0),
    .in6(sllx_out), .in7(sltx_out), .in8(divu0), .in9(remu0), .in10(mul0), .in11(mulhu0), .in12(sub0),
    .in13(lui0), .in14(mulh0), .out(ALUSel));  // open: in15, gs, en_out, en_in
  not not_190 (not_190_out, instr[2]);
  not not_191 (not_191_out, instr[3]);
  not not_192 (not_192_out, instr[6]);
  not not_193 (not_193_out, instr[13]);
  not not_194 (not_194_out, instr[14]);
  not not_195 (not_195_out, instr[26]);
  not not_196 (not_196_out, instr[27]);
  not not_197 (not_197_out, instr[28]);
  not not_198 (not_198_out, instr[29]);
  not not_199 (not_199_out, instr[30]);
  not not_200 (not_200_out, instr[31]);
  not not_201 (not_201_out, instr[2]);
  not not_202 (not_202_out, instr[3]);
  not not_203 (not_203_out, instr[6]);
  not not_204 (not_204_out, instr[12]);
  not not_205 (not_205_out, instr[25]);
  not not_206 (not_206_out, instr[26]);
  not not_207 (not_207_out, instr[27]);
  not not_208 (not_208_out, instr[28]);
  not not_209 (not_209_out, instr[29]);
  not not_210 (not_210_out, instr[30]);
  not not_211 (not_211_out, instr[31]);
  not not_212 (not_212_out, instr[2]);
  not not_213 (not_213_out, instr[3]);
  not not_214 (not_214_out, instr[5]);
  not not_215 (not_215_out, instr[6]);
  not not_216 (not_216_out, instr[12]);
  not not_217 (not_217_out, instr[13]);
  not not_218 (not_218_out, instr[14]);
  not not_219 (not_219_out, instr[2]);
  not not_220 (not_220_out, instr[3]);
  not not_221 (not_221_out, instr[5]);
  not not_222 (not_222_out, instr[6]);
  not not_223 (not_223_out, instr[12]);
  not not_224 (not_224_out, instr[2]);
  not not_225 (not_225_out, instr[3]);
  not not_226 (not_226_out, instr[4]);
  not not_227 (not_227_out, instr[13]);
  not not_228 (not_228_out, instr[14]);
  and and_28 (mulh0, instr[0], instr[1], not_190_out, not_191_out, instr[4], instr[5], not_192_out, instr[12], not_193_out, not_194_out, instr[25], not_195_out, not_196_out, not_197_out, not_198_out, not_199_out, not_200_out);
  and and_29 (or0, instr[0], instr[1], not_201_out, not_202_out, instr[4], instr[5], not_203_out, not_204_out, instr[13], instr[14], not_205_out, not_206_out, not_207_out, not_208_out, not_209_out, not_210_out, not_211_out);
  and and_30 (addi0, instr[0], instr[1], not_212_out, not_213_out, instr[4], not_214_out, not_215_out, not_216_out, not_217_out, not_218_out);
  and and_31 (ori0, instr[0], instr[1], not_219_out, not_220_out, instr[4], not_221_out, not_222_out, not_223_out, instr[13], instr[14]);
  and and_32 (bne0, instr[0], instr[1], not_224_out, not_225_out, not_226_out, instr[5], instr[6], instr[12], not_227_out, not_228_out);
  Priority_Encoder #(.select(2)) priority_encoder_3 (
    .in0(lw0), .in1(lh0), .in2(lb0), .out(LSel));  // open: in3, gs, en_out, en_in
  or or_9 (or_9_out, add0, mul0, sub0, sll0, mulh0, mulhu0, slt0, xor0, divu0, srl0, or0, remu0, and0, slti0, addi0, xori0, andi0, lui0, slli0, srli0, srai0, ori0);
  not not_229 (not_229_out, instr[2]);
  not not_230 (not_230_out, instr[3]);
  not not_231 (not_231_out, instr[6]);
  not not_232 (not_232_out, instr[14]);
  not not_233 (not_233_out, instr[26]);
  not not_234 (not_234_out, instr[27]);
  not not_235 (not_235_out, instr[28]);
  not not_236 (not_236_out, instr[29]);
  not not_237 (not_237_out, instr[30]);
  not not_238 (not_238_out, instr[31]);
  not not_239 (not_239_out, instr[2]);
  not not_240 (not_240_out, instr[3]);
  not not_241 (not_241_out, instr[6]);
  not not_242 (not_242_out, instr[26]);
  not not_243 (not_243_out, instr[27]);
  not not_244 (not_244_out, instr[28]);
  not not_245 (not_245_out, instr[29]);
  not not_246 (not_246_out, instr[30]);
  not not_247 (not_247_out, instr[31]);
  not not_248 (not_248_out, instr[2]);
  not not_249 (not_249_out, instr[3]);
  not not_250 (not_250_out, instr[5]);
  not not_251 (not_251_out, instr[6]);
  not not_252 (not_252_out, instr[13]);
  not not_253 (not_253_out, instr[14]);
  not not_254 (not_254_out, instr[25]);
  not not_255 (not_255_out, instr[26]);
  not not_256 (not_256_out, instr[27]);
  not not_257 (not_257_out, instr[28]);
  not not_258 (not_258_out, instr[29]);
  not not_259 (not_259_out, instr[30]);
  not not_260 (not_260_out, instr[31]);
  not not_261 (not_261_out, instr[2]);
  not not_262 (not_262_out, instr[3]);
  not not_263 (not_263_out, instr[5]);
  not not_264 (not_264_out, instr[6]);
  not not_265 (not_265_out, instr[3]);
  not not_266 (not_266_out, instr[6]);
  or or_10 (or_10_out, jal0, jalr0);
  or or_11 (or_11_out, lb0, lh0, lw0);
  Priority_Encoder #(.select(2)) priority_encoder_4 (
    .in0(or_10_out), .in1(or_9_out), .in2(or_11_out), .out(WBSel));  // open: in3, gs, en_out, en_in
  and and_33 (mulhu0, instr[0], instr[1], not_229_out, not_230_out, instr[4], instr[5], not_231_out, instr[12], instr[13], not_232_out, instr[25], not_233_out, not_234_out, not_235_out, not_236_out, not_237_out, not_238_out);
  and and_34 (remu0, instr[0], instr[1], not_239_out, not_240_out, instr[4], instr[5], not_241_out, instr[12], instr[13], instr[14], instr[25], not_242_out, not_243_out, not_244_out, not_245_out, not_246_out, not_247_out);
  and and_35 (slli0, instr[0], instr[1], not_248_out, not_249_out, instr[4], not_250_out, not_251_out, instr[12], not_252_out, not_253_out, not_254_out, not_255_out, not_256_out, not_257_out, not_258_out, not_259_out, not_260_out);
  and and_36 (andi0, instr[0], instr[1], not_261_out, not_262_out, instr[4], not_263_out, not_264_out, instr[12], instr[13], instr[14]);
  and and_37 (lui0, instr[0], instr[1], instr[2], not_265_out, instr[4], instr[5], not_266_out);

  // Other names for the same wires on the sheet: bltu0 = BrUn; UJtype = jal0; Utype = lui0; Stype = MemRW;
  //   sw0 = MemRW
endmodule
