// Logisim project CPU-alltest.circ as structural Verilog: 1 circuit, main circuit main
module main (
  output [31:0] ra,
  output [31:0] sp,
  output [31:0] t0,
  output [31:0] t1,
  output [31:0] t2,
  output [31:0] s0,
  output [31:0] s1,
  output [31:0] a0,
  output [31:0] Requested_Address,
  output [31:0] Requested_Instruction,
  output [15:0] Time_Step,
  output halt
);

  wire clk;

  Clock clock_1 (.out(clk));
  // Probe on Requested_Address
  ROM #(.addrWidth(14), .dataWidth(32)) rom_1 (.addr(Requested_Address[15:2]), .data(Requested_Instruction));
  cpu_main main_1 (
    .INSTRUCTION(Requested_Instruction), .CLOCK(clk), .ra(ra), .sp(sp), .t0(t0), .t1(t1), .t2(t2), .s0(s0),
    .s1(s1), .a0(a0), .PROGRAM_COUNTER(Requested_Address));
  // Probe on Requested_Instruction
  Counter #(.width(16), .max('hffff)) counter_1 (.clk(clk), .Q(Time_Step));  // open: clr, load, up, count, D, carry
  Comparator #(.width(16)) comparator_1 (.a(Time_Step), .b(16'h5b), .eq(halt));  // open: gt, lt

  // Other names for the same wires on the sheet: fetch_addr[31:0] = Requested_Address;
  //   Instruction[31:0] = Requested_Instruction

  // Notes on the sheet:
  //   contents of rom_1 (hex, n*v repeats v):
  //   7FF48313 D4430393 005303B3 00700333 02628333 02730033 02030533 02539333 02731033 0262B3B3 0052C333
  //   0072C333 005323B3 00702333 40630333 405303B3 0003D333 000053B3 005353B3 005313B3 00001033 000313B3
  //   0053E333 00706333 00636333 00730533 006504B3 FFC10113 00410113 00A403B3 0053F333 00707333 00637333
  //   00229313 00331513 00031393 01D31393 00102513 00232513 00002013 00234513 00A04513 0043D313 0003D293
  //   01C55513 00235013 4043D313 4003D293 41455513 40235013 0043E313 0003E293 06456513 00236013 0043F313
  //   0003F293 06457513 00237013 1E1632B7 03025337 00038293 00300013 80000313 0253D333 0203D333 0203F333
  //   0253F333 7D000313 00732023 00A32823 00400313 00432403 00831403 00231403 00431403 00230403 00030403
  //   00130403 00330403 00100293 00100313 00628263 124000EF FFF00293 00100313 FE628AE3 00100293 00200313
  //   FE6284E3 00100293 00200313 FC62CEE3 000282B3 00030333 FC62C8E3 00200293 00100313 FC62C2E3 000282B3
  //   00030333 FA62CCE3 FFE00293 00100313 FA62C6E3 000282B3 00030333 FA62C0E3 00100293 00100313 F862CAE3
  //   000282B3 00030333 F862C4E3 00100293 00200313 F662CEE3 000282B3 00030333 F662C8E3 00200293 00100313
  //   F662E2E3 000282B3 00030333 F462ECE3 00100293 00100313 F462E6E3 000282B3 00030333 F462E0E3 00100293
  //   00200313 F262EAE3 000282B3 00030333 F262E4E3 00200293 00100313 F0629EE3 000282B3 00030333 F06298E3
  //   00100293 00100313 F06292E3 000282B3 00030333 EE629CE3 FFF00293 FFF00313 EE6296E3 000282B3 00030333
  //   EE6290E3 004000EF 00408067
  //   YOUR CPU SHOULD FIT IN HERE!
  //   Instruction Memory
  //   Halts Execution After Constant # of Clock Cycles
  //   Constant
endmodule
