// Logisim project cpu.circ as structural Verilog: 1 circuit, main circuit main
module main (
  input  [31:0] INSTRUCTION,
  input  CLOCK,
  output [31:0] PROGRAM_COUNTER,
  output [31:0] ra,
  output [31:0] sp,
  output [31:0] t0,
  output [31:0] t1,
  output [31:0] t2,
  output [31:0] s0,
  output [31:0] s1,
  output [31:0] a0
);

  wire DMEM_p1, DMEM_p2, DMEM_p5;
  wire [31:0] adder_1_out, Arithmetic_Logic_Unit_result, bit_extender_1_out, DMEM_p7, multiplexer_1_out,
       multiplexer_2_out, pipelined, RegFile_read_data_1, RegFile_read_data_2;

  Adder #(.width(32)) adder_1 (.a(PROGRAM_COUNTER), .b(32'h4), .out(adder_1_out));  // open: cin, cout
  Register #(.width(32)) PC (.D(adder_1_out), .en(1'b1), .clk(CLOCK), .Q(PROGRAM_COUNTER));  // open: clr
  Register #(.width(32)) register_1 (.D(INSTRUCTION), .en(1'b1), .clk(CLOCK), .Q(pipelined));  // open: clr
  assign bit_extender_1_out = {{20{pipelined[31]}}, pipelined[31:20]};  // Bit_Extender bit_extender_1
  regfile_main RegFile (
    .rs2(pipelined[24:20]), .rd(pipelined[11:7]), .Read_Data_1(RegFile_read_data_1),
    .Read_Data_2(RegFile_read_data_2), .ra(ra), .sp(sp), .t0(t0), .t1(t1), .t2(t2), .s0(s0), .s1(s1),
    .a0(a0), .rs1(pipelined[19:15]), .Write_Data(multiplexer_2_out), .RegWEn(1'b1), .clk(CLOCK));
  Multiplexer #(.width(32), .enable("false")) multiplexer_1 (
    .in0(RegFile_read_data_2), .in1(bit_extender_1_out), .out(multiplexer_1_out), .sel(1'b1));
  alu Arithmetic_Logic_Unit (
    .Result(Arithmetic_Logic_Unit_result), .ALUSel(4'b0000), .A(RegFile_read_data_1), .B(multiplexer_1_out));
  // mem_main DMEM: pin names not known; wires that end beside it: DMEM_p1, DMEM_p2, CLOCK, DMEM_p2, DMEM_p5, 1'b0, DMEM_p7
  Multiplexer #(.select(2), .width(32), .enable("false")) multiplexer_2 (
    .in1(Arithmetic_Logic_Unit_result), .in2(DMEM_p7), .out(multiplexer_2_out), .sel(2'b01));  // open: in0, in3

  // Other names for the same wires on the sheet: clk = CLOCK

  // Notes on the sheet:
  //   Output
  //   IMEM (do **NOT** move this)
  //   Inputs
  //   It is OK to move the PC, RegFile, ALU, and MEM to wherever is most convenient for you when constructing your CPU, and to delete this text
  //   Inputs/Outputs for testing. Do **NOT** move these.
endmodule
