// Logisim project alu.circ as structural Verilog: 1 circuit, main circuit alu
module alu (
  input  [31:0] A,
  input  [31:0] B,
  input  [3:0] ALUSel,
  output [31:0] Result
);

  wire comparator_1_lt;
  wire [31:0] add0, adder_2_out, and1, bit_extender_1_out, bit_extender_2_out, bsel13, divu8, mul10, mulh14,
       mulhu11, multiplier_1_cout, multiplier_4_out, multiplier_5_out, or2, remu9, sll6, slt7, sra5, srl4,
       sub12, xor3;

  Multiplier #(.width(32)) multiplier_1 (.a(A), .b(B), .cout(multiplier_1_cout));  // open: out, cin
  Adder #(.width(32)) adder_1 (.a(A), .b(B), .out(add0));  // open: cin, cout
  assign and1 = A & B;  // AND_Gate and_1, 32 bits wide
  assign or2 = A | B;  // OR_Gate or_1, 32 bits wide
  assign xor3 = A ^ B;  // XOR_Gate xor_1, 32 bits wide
  Shifter #(.width(32), .shift("lr")) shifter_1 (.in(A), .\dist (B[4:0]), .out(srl4));
  Shifter #(.width(32), .shift("ar")) shifter_2 (.in(A), .\dist (B[4:0]), .out(sra5));
  Shifter #(.width(32)) shifter_3 (.in(A), .\dist (B[4:0]), .out(sll6));
  Comparator #(.width(32)) comparator_1 (.a(A), .b(B), .lt(comparator_1_lt));  // open: gt, eq
  Divider #(.width(32)) divider_1 (.a(A), .b(B), .out(divu8));  // open: upper, rem
  Divider #(.width(32)) divider_2 (.a(A), .b(B), .rem(remu9));  // open: out, upper
  Multiplier #(.width(32)) multiplier_2 (.a(A), .b(B), .out(mul10));  // open: cin, cout
  Multiplier #(.width(32)) multiplier_3 (.a(A), .b(B), .cout(mulhu11));  // open: out, cin
  Subtractor #(.width(32)) subtractor_1 (.a(A), .b(B), .out(sub12));  // open: bin, bout
  Multiplexer #(.width(32), .enable("false")) multiplexer_1 (.in0(A), .in1(B), .out(bsel13), .sel(1'b1));
  assign bit_extender_1_out = {{31{A[31]}}, A[31]};  // Bit_Extender bit_extender_1
  assign bit_extender_2_out = {{31{B[31]}}, B[31]};  // Bit_Extender bit_extender_2
  assign slt7 = {{31{1'b0}}, comparator_1_lt};  // Bit_Extender bit_extender_3
  Multiplier #(.width(32)) multiplier_4 (.a(B), .b(bit_extender_1_out), .out(multiplier_4_out));  // open: cin, cout
  Multiplier #(.width(32)) multiplier_5 (.a(bit_extender_2_out), .b(A), .out(multiplier_5_out));  // open: cin, cout
  Adder #(.width(32)) adder_2 (.a(multiplier_1_cout), .b(multiplier_5_out), .out(adder_2_out));  // open: cin, cout
  Adder #(.width(32)) adder_3 (.a(multiplier_4_out), .b(adder_2_out), .out(mulh14));  // open: cin, cout
  Multiplexer #(.select(4), .width(32), .enable("false")) multiplexer_2 (
    .in0(add0), .in1(and1), .in2(or2), .in3(xor3), .in4(srl4), .in5(sra5), .in6(sll6), .in7(slt7),
    .in8(divu8), .in9(remu9), .in10(mul10), .in11(mulhu11), .in12(sub12), .in13(bsel13), .in14(mulh14),
    .out(Result), .sel(ALUSel));  // open: in15

  // Notes on the sheet:
  //   INPUTS to your circuit
  //   DON'T CHANGE THE LOCATIONS OF THE INPUTS AND OUTPUTS!
  //   OUTPUT from your circuit
endmodule
